# Fritzing sketch Circuit Sketch (saved by Fritzing 0.9.3b)
breadboards: 1

parts:
  J1 = Basic Servo
  J2 = Basic Servo
  J4 = Basic Servo
  J5 = Basic Servo
  J6 = Basic Servo
  Part1 = Arduino Uno (Rev3) - ICSP
  BAT1 = BC9VPC [package=bc9vpc]
  J7 = Basic Servo
  Part3 = Bluetooth HC-05 Macho
  Part4 = HC-SR04 Ultrasonic Rangemeter
  LED1 = LED - 5mm [color="Red (633nm)" package="5 mm [THT]"]

nets:
  GND: J1.gnd, J2.gnd, J4.gnd, J5.gnd, J6.gnd, Part1.GND, BAT1.V-, J7.gnd, Part3.GND, Part4.GND, LED1.cathode
  N1: J1.pulse, J2.pulse, Part1.D7, J7.pulse
  VCC: J2.vcc, J4.vcc, J5.vcc, J6.vcc, J7.vcc, Part3.VCC, Part4.VCC
  N2: J4.pulse, J5.pulse, J6.pulse, Part1.D6_PWM
  N3: Part1.D8, LED1.anode
  N4: Part1.D0/RX, Part3.TXD
  N5: Part1.D1/TX, Part3.RXD
  N6: Part1.D2, Part4.Echo
  N7: Part1.D3_PWM, Part4.Trig
